# Fritzing sketch P1_Meter_Schematic (saved by Fritzing 0.9.4)
breadboards: 1

parts:
  Q1 = PNP-Transistor [part_number=BS170 package="TO92 [THT]"]
  Part1 = SparkFun ESP8266 Thing
  J1 = RJ9 [package=rj9]
  R1 = Resistor [tolerance=±1% resistance=10k package="0805 [SMD]"]
  R2 = Resistor [tolerance=±1% resistance=10k package="0805 [SMD]"]

nets:
  N1: Q1.E, Part1.U0RXI, R1.Pin_1
  N2: Q1.B, J1.4, R2.Pin_1
  N3: Q1.C, Part1.GND, J1.2
  N4: Part1.USBVCC, J1.1, R1.Pin_0, R2.Pin_0

notes:
  1x BS170
  2x 10K ohm
